// Logisim project alu.circ as structural Verilog: 8 circuits, main circuit main
module main (
  input  [3:0] ALUcontrol,
  input  [3:0] a,
  input  [3:0] b,
  output [3:0] Result,
  output Zero,
  output Overflow
);

  _4_bit_ALU__full u_4_bit_alu_full_1 (
    .ALUcontrol(ALUcontrol), .a(a), .b(b), .Result(Result), .Zero(Zero), .Overflow(Overflow));
endmodule

module _1_bit_adder (
  input  CarryIn,
  input  a,
  input  b,
  output CarryOut,
  output Sum
);

  wire and_1_out, and_2_out, and_3_out, and_4_out, xor_1_out;

  and and_1 (and_1_out, CarryIn, a);
  and and_2 (and_2_out, CarryIn, b);
  and and_3 (and_3_out, a, b);
  ExactlyOne xor_1 (.out(xor_1_out), .in0(CarryIn), .in1(a), .in2(b));
  and and_4 (and_4_out, CarryIn, a, b);
  or or_1 (Sum, xor_1_out, and_4_out);
  or or_2 (CarryOut, and_1_out, and_2_out, and_3_out);
endmodule

module _1_bit_ALU (
  input  Ainvert,
  input  Binvert,
  input  a,
  input  b,
  input  Less,
  input  [1:0] Operation,
  input  CarryIn,
  output Result,
  output CarryOut
);

  wire and_1_out, multiplexer_1_out, multiplexer_2_out, n1_bit_adder_1_sum, not_1_out, not_2_out, or_1_out;

  Multiplexer multiplexer_1 (.in0(a), .in1(not_1_out), .out(multiplexer_1_out), .sel(Ainvert));
  not not_1 (not_1_out, a);
  Multiplexer multiplexer_2 (.in0(b), .in1(not_2_out), .out(multiplexer_2_out), .sel(Binvert));
  not not_2 (not_2_out, b);
  _1_bit_adder u_1_bit_adder_1 (
    .CarryIn(CarryIn), .a(multiplexer_1_out), .b(multiplexer_2_out), .CarryOut(CarryOut),
    .Sum(n1_bit_adder_1_sum));
  and and_1 (and_1_out, multiplexer_1_out, multiplexer_2_out);
  or or_1 (or_1_out, multiplexer_1_out, multiplexer_2_out);
  Multiplexer #(.select(2)) multiplexer_3 (
    .in0(and_1_out), .in1(or_1_out), .in2(n1_bit_adder_1_sum), .in3(Less), .out(Result), .sel(Operation));
endmodule

module _4_bit_ALU (
  input  Ainvert,
  input  Bnegate,
  input  [1:0] Operation,
  input  [3:0] a,
  input  [3:0] b,
  output [3:0] Result,
  output Zero,
  output Overflow
);

  wire n1_bit_alu_1_carryout, n1_bit_alu_1_result, n1_bit_alu_2_carryout, n1_bit_alu_2_result,
       n1_bit_alu_3_carryout, n1_bit_alu_3_result, n1_bit_alu_last_1_result, n1_bit_alu_last_1_set,
       select_4_bits_1__0, select_4_bits_1__1, select_4_bits_1__2, select_4_bits_1__3, select_4_bits_2__0,
       select_4_bits_2__1, select_4_bits_2__2, select_4_bits_2__3;

  Select_4_bits select_4_bits_1 (
    .\input (a), ._0(select_4_bits_1__0), ._1(select_4_bits_1__1), ._2(select_4_bits_1__2),
    ._3(select_4_bits_1__3));
  Select_4_bits select_4_bits_2 (
    .\input (b), ._0(select_4_bits_2__0), ._1(select_4_bits_2__1), ._2(select_4_bits_2__2),
    ._3(select_4_bits_2__3));
  _1_bit_ALU u_1_bit_alu_1 (
    .a(select_4_bits_1__0), .b(select_4_bits_2__0), .CarryIn(Bnegate), .Ainvert(Ainvert), .Binvert(Bnegate),
    .CarryOut(n1_bit_alu_1_carryout), .Less(n1_bit_alu_last_1_set), .Operation(Operation),
    .Result(n1_bit_alu_1_result));
  _1_bit_ALU u_1_bit_alu_2 (
    .a(select_4_bits_1__1), .b(select_4_bits_2__1), .CarryIn(n1_bit_alu_1_carryout), .Ainvert(Ainvert),
    .Binvert(Bnegate), .CarryOut(n1_bit_alu_2_carryout), .Less(1'b0), .Operation(Operation),
    .Result(n1_bit_alu_2_result));
  _1_bit_ALU u_1_bit_alu_3 (
    .a(select_4_bits_1__2), .b(select_4_bits_2__2), .CarryIn(n1_bit_alu_2_carryout), .Ainvert(Ainvert),
    .Binvert(Bnegate), .CarryOut(n1_bit_alu_3_carryout), .Less(1'b0), .Operation(Operation),
    .Result(n1_bit_alu_3_result));
  _1_bit_ALU__last u_1_bit_alu_last_1 (
    .a(select_4_bits_1__3), .b(select_4_bits_2__3), .CarryIn(n1_bit_alu_3_carryout), .Ainvert(Ainvert),
    .Binvert(Bnegate), .Overflow(Overflow), .Less(1'b0), .Operation(Operation),
    .Result(n1_bit_alu_last_1_result), .Set(n1_bit_alu_last_1_set));
  Make_4_bit_int make_4_bit_int_1 (
    ._0(n1_bit_alu_1_result), ._1(n1_bit_alu_2_result), ._2(n1_bit_alu_3_result),
    ._3(n1_bit_alu_last_1_result), .\output (Result));
  nor nor_1 (Zero, n1_bit_alu_1_result, n1_bit_alu_2_result, n1_bit_alu_3_result, n1_bit_alu_last_1_result);
endmodule

module _1_bit_ALU__last (
  input  Ainvert,
  input  Binvert,
  input  a,
  input  b,
  input  Less,
  input  [1:0] Operation,
  input  CarryIn,
  output Result,
  output Set,
  output Overflow
);

  wire and_1_out, multiplexer_1_out, multiplexer_2_out, n1_bit_adder_1_carryout, not_1_out, not_2_out,
       or_1_out;

  Multiplexer multiplexer_1 (.in0(a), .in1(not_1_out), .out(multiplexer_1_out), .sel(Ainvert));
  not not_1 (not_1_out, a);
  Multiplexer multiplexer_2 (.in0(b), .in1(not_2_out), .out(multiplexer_2_out), .sel(Binvert));
  not not_2 (not_2_out, b);
  _1_bit_adder u_1_bit_adder_1 (
    .CarryIn(CarryIn), .a(multiplexer_1_out), .b(multiplexer_2_out), .CarryOut(n1_bit_adder_1_carryout),
    .Sum(Set));
  xor xor_1 (Overflow, CarryIn, n1_bit_adder_1_carryout);
  and and_1 (and_1_out, multiplexer_1_out, multiplexer_2_out);
  or or_1 (or_1_out, multiplexer_1_out, multiplexer_2_out);
  Multiplexer #(.select(2)) multiplexer_3 (
    .in0(and_1_out), .in1(or_1_out), .in2(Set), .in3(Less), .out(Result), .sel(Operation));

  // Notes on the sheet:
  //   Se opgave C.15
endmodule

module Select_4_bits (
  input  [3:0] \input ,
  output _0,
  output _1,
  output _2,
  output _3
);

  // PLA #(.in_width(4), .out_width(1), .truth_table("xxx1,1#")) pla_1: pin names not known; wires that end beside it: _0
  // PLA #(.in_width(4), .out_width(1), .truth_table("xx1x,1#")) pla_2: pin names not known; wires that end beside it: _1
  // PLA #(.in_width(4), .out_width(1), .truth_table("x1xx,1#")) pla_3: pin names not known; wires that end beside it: _2
  // PLA #(.in_width(4), .out_width(1), .truth_table("1xxx,1#")) pla_4: pin names not known; wires that end beside it: _3
endmodule

module Make_4_bit_int (
  input  _0,
  input  _1,
  input  _2,
  input  _3,
  output [3:0] \output 
);

  wire [3:0] pla_1_p1, pla_2_p1, pla_3_p1, pla_4_p1;

  // PLA #(.in_width(1), .out_width(4), .truth_table("1,0001#")) pla_1: pin names not known; wires that end beside it: pla_1_p1
  // PLA #(.in_width(1), .out_width(4), .truth_table("1,0010#")) pla_2: pin names not known; wires that end beside it: pla_2_p1
  // PLA #(.in_width(1), .out_width(4), .truth_table("1,0100#")) pla_3: pin names not known; wires that end beside it: pla_3_p1
  // PLA #(.in_width(1), .out_width(4), .truth_table("1,1000#")) pla_4: pin names not known; wires that end beside it: pla_4_p1
  assign \output  = pla_1_p1 | pla_2_p1 | pla_3_p1 | pla_4_p1;  // OR_Gate or_1, 4 bits wide
endmodule

module _4_bit_ALU__full (
  input  [3:0] ALUcontrol,
  input  [3:0] a,
  input  [3:0] b,
  output [3:0] Result,
  output Zero,
  output Overflow
);

  wire pla_2_p1, pla_3_out;
  wire [1:0] pla_1_p1;

  // PLA #(.in_width(4), .truth_table("0010,10#add\n0110,10#sub\n0000,00#AND\n0001,01#OR\n0111,11#slt\n1100,01#NOR")) pla_1: pin names not known; wires that end beside it: pla_1_p1
  // PLA #(.in_width(4), .out_width(1), .truth_table("0110,1#sub\n1100,1#NOR")) pla_2: pin names not known; wires that end beside it: pla_2_p1
  PLA #(.in_width(4), .out_width(1), .truth_table("1100,1#NOR")) pla_3 (.out(pla_3_out));  // open: in
  _4_bit_ALU u_4_bit_alu_1 (
    .a(a), .b(b), .Ainvert(pla_3_out), .Bnegate(pla_2_p1), .Operation(pla_1_p1), .Result(Result),
    .Zero(Zero), .Overflow(Overflow));

  // Notes on the sheet:
  //   TODO: Fix slt and test det hele (overflow detection virker vist ikke).
endmodule
