// Logisim project single_cycle.circ as structural Verilog: 5 circuits, main circuit main
module Control (
  input  [5:0] Instruction,
  output [1:0] BranchOp,
  output RegDst,
  output SignedIMM,
  output ALUSrc,
  output MemWrite,
  output MemRead,
  output MemToReg,
  output RegWrite,
  output [1:0] AluOp
);

  PLA #(.in_width(6), .out_width(11), .truth_table("000000,00100000100#R-format\n000100,10000000000#beq\n000101,11000000000#bne\n001000,00011000100#addi\n001001,00001000100#addiu\n001010,00011000100#slti\n001011,00001000100#sltiu\n001100,00001000100#andi\n001101,00001000100#ori\n100011,00011011000#lw\n101011,00011100000#sw")) PLA_backup ();  // open: in, out
  PLA #(.in_width(6), .out_width(11), .truth_table("000000,00100000110#R-format\n000100,10000000001#beq\n000101,11000000001#bne\n001000,00011000111#addi\n001001,00001000111#addiu\n001010,00011000111#slti\n001100,00001000111#andi\n001101,00001000111#ori\n100011,00011011000#lw\n101011,00011100000#sw")) pla_1 ();  // open: in, out
endmodule

module ALU_control (
  input  [1:0] ALUop,
  input  [2:0] IMM_OP,
  input  [5:0] Funct,
  output [3:0] Output
);

  // PLA #(.in_width(11), .out_width(4), .truth_table("10001110xxx,0110#subu\n10010010xxx,0000#and\n10010110xxx,0001#or\n10000110xxx,0010#addu\n10101010xxx,0111#slt\nxxxxxx00001,0010#addiu\nxxxxxx00100,0000#andi\nxxxxxx00101,0001#ori\nxxxxxx00010,0111#slti\nxxxxxx01xxx,0110#beq\nxxxxxx00xxx,0010#sw\nxxxxxx00xxx,0010#lw")) pla_1: pin names not known; wires that end beside it: Output
endmodule

module Bit_extender (
  input  [15:0] Input,
  input  Signed,
  output [31:0] Output
);

  and and_1 (Output[31], Input[15], Signed);

  assign Output[30:0] = {{15{Output[31]}}, Input};
endmodule

module main (
);

  wire clock_1_out, control_1_alusrc, control_1_memread, control_1_memtoreg, control_1_memwrite,
       control_1_regdst, control_1_signedimm, mips_alu_1_p3, mipsprogramrom_1_p5, registerfile_1_p5;
  wire [1:0] control_1_aluop, control_1_branchop;
  wire [3:0] alu_control_1_output;
  wire [4:0] multiplexer_1_out;
  wire [15:0] mipsprogramrom_1_p2, mipsprogramrom_1_p2_2;
  wire [31:0] bit_extender_1_output, branch_control_1_addressout, mips_alu_1_p4, mips_ram_1_p6,
       mipsprogramrom_1_p3, register_1_q, registerfile_1_p6, registerfile_1_p7;

  Branch_Control branch_control_1 (
    .AddressOut(branch_control_1_addressout), .AddressIn(register_1_q), .Zero(mips_alu_1_p3),
    .BranchOp(control_1_branchop), .Difference(mipsprogramrom_1_p2));
  Register #(.width(32)) register_1 (
    .D(branch_control_1_addressout), .en(1'b1), .Q(register_1_q), .clk(clock_1_out));  // open: clr
  Clock clock_1 (.out(clock_1_out));
  // MIPSProgramROM mipsprogramrom_1: pin names not known; wires that end beside it: register_1_q, {mipsprogramrom_1_p2_2, mipsprogramrom_1_p2}, mipsprogramrom_1_p3, clock_1_out, mipsprogramrom_1_p5
  Control control_1 (
    .Instruction(mipsprogramrom_1_p2_2[15:10]), .BranchOp(control_1_branchop), .RegDst(control_1_regdst),
    .SignedIMM(control_1_signedimm), .ALUSrc(control_1_alusrc), .MemWrite(control_1_memwrite),
    .MemRead(control_1_memread), .MemToReg(control_1_memtoreg), .RegWrite(mipsprogramrom_1_p5),
    .AluOp(control_1_aluop));
  Multiplexer #(.width(5)) multiplexer_1 (
    .in0(mipsprogramrom_1_p2_2[4:0]), .in1(mipsprogramrom_1_p2[15:11]), .out(multiplexer_1_out),
    .sel(control_1_regdst));
  // RegisterFile registerfile_1: pin names not known; wires that end beside it: multiplexer_1_out, mipsprogramrom_1_p2_2[4:0], mipsprogramrom_1_p2_2[9:5], mipsprogramrom_1_p2_2[4:0], registerfile_1_p5, registerfile_1_p6, registerfile_1_p7
  Bit_extender bit_extender_1 (
    .Input(mipsprogramrom_1_p2), .Signed(control_1_signedimm), .Output(bit_extender_1_output));
  ALU_control alu_control_1 (
    .ALUop(control_1_aluop), .IMM_OP(mipsprogramrom_1_p2_2[12:10]), .Funct(mipsprogramrom_1_p2[5:0]),
    .Output(alu_control_1_output));
  // Mips_ALU mips_alu_1: pin names not known; wires that end beside it: registerfile_1_p5, alu_control_1_output, mips_alu_1_p3, mips_alu_1_p4
  Multiplexer #(.width(32)) multiplexer_2 (
    .in0(registerfile_1_p6), .in1(bit_extender_1_output), .out(registerfile_1_p7), .sel(control_1_alusrc));
  Multiplexer #(.width(32)) multiplexer_3 (
    .in0(mips_alu_1_p4), .in1(mips_ram_1_p6), .out(mipsprogramrom_1_p3), .sel(control_1_memwrite));
  // MIPS_RAM #(.addrWidth(24)) mips_ram_1: pin names not known; wires that end beside it: mips_alu_1_p4[23:0], registerfile_1_p6, control_1_memread, control_1_memtoreg, clock_1_out, mips_ram_1_p6

  // Notes on the sheet:
  //   contents of mipsprogramrom_1 (hex, n*v repeats v):
  //   LABEL1:     beq $t0, $t0, LABEL2     addiu $1, $0, 0x1      # $1 = 0x1     addiu $2, $0, 0xc      #
  //   $2 = 0xc     addiu $3, $0, 0xffff   # $3 = 0xffffffff     addu  $4, $1, $2       # $4 = 0xd     subu
  //   $5, $2, $1       # $5 = 0xb     subu  $6, $1, $2       # $6 = 0xfffffff5 LABEL2:     beq $t0, $t0,
  //   LABEL1
endmodule

module Branch_Control (
  input  Zero,
  input  [1:0] BranchOp,
  input  [31:0] AddressIn,
  input  [15:0] Difference,
  output [31:0] AddressOut
);

  wire and_1_out, xor_1_out;
  wire [31:0] adder_1_out, adder_2_out, bit_extender_1_output, shifter_1_out;

  Multiplexer #(.width(32)) multiplexer_1 (.in0(AddressIn), .in1(adder_2_out), .out(AddressOut), .sel(and_1_out));
  and and_1 (and_1_out, xor_1_out, BranchOp[0]);
  xor xor_1 (xor_1_out, Zero, BranchOp[1]);
  Adder #(.width(32)) adder_1 (.a(AddressIn), .b(32'h4), .out(adder_1_out));  // open: cin, cout
  Bit_extender bit_extender_1 (.Input(Difference), .Signed(1'b1), .Output(bit_extender_1_output));
  Shifter #(.width(32)) shifter_1 (.in(bit_extender_1_output), .\dist (5'b00010), .out(shifter_1_out));
  Adder #(.width(32)) adder_2 (.a(adder_1_out), .b(shifter_1_out), .out(adder_2_out));  // open: cin, cout
endmodule
